// Logisim project cpu.circ as structural Verilog
module ALU (
  input  [7:0] Operand_1,
  input  [7:0] Operand_2,
  input  [2:0] in_3,
  output [7:0] ALU_Output,
  output OF,
  output NZ
);

  wire AOF, SOF;
  wire [7:0] ADD, AND, JMP, NOT, OR, XOR;

  assign AND = Operand_1 & Operand_2;  // AND_Gate and_1, 8 bits wide
  assign OR = Operand_1 | Operand_2;  // OR_Gate or_1, 8 bits wide
  assign XOR = Operand_1 ^ Operand_2;  // XOR_Gate xor_1, 8 bits wide
  assign NOT = ~Operand_1;  // NOT_Gate not_1, 8 bits wide
  Adder adder_1 (.a(Operand_1), .b(Operand_2), .out(ADD), .cout(AOF));  // open: cin
  Subtractor subtractor_1 (.a(Operand_1), .b(Operand_2), .out(JMP), .bout(SOF));  // open: bin
  Multiplexer #(.select(3), .width(8), .enable("false")) multiplexer_1 (
    .in1(ADD), .in2(JMP), .in3(JMP), .in4(AND), .in5(OR), .in6(NOT), .in7(XOR), .out(ALU_Output), .sel(in_3));  // open: in0
  Multiplexer #(.enable("false")) multiplexer_2 (.in0(AOF), .in1(SOF), .out(OF), .sel(in_3[1]));
  or or_2 (NZ, ALU_Output[7], ALU_Output[6], ALU_Output[5], ALU_Output[4], ALU_Output[3], ALU_Output[2], ALU_Output[1], ALU_Output[0]);

  // Other names for the same wires on the sheet: _3_Bit_op_code[2:0] = in_3; A[7:0] = Operand_1; B[7:0] = Operand_2;
  //   SUB[7:0] = JMP
endmodule
